// Logisim project masinadespalatvase.circ as structural Verilog
module main (
  input  Start,
  input  door,
  input  rst,
  input  manualsw,
  input  prewashsw,
  input  extrarinsesw,
  input  Clk100MHZ,
  input  ButonTemp,
  input  Mod1,
  input  Mod2,
  input  Mod3,
  input  [2:0] SwitchTemp,
  input  Mod4,
  output doorled,
  output pwled,
  output erled,
  output [3:0] anod,
  output [4:0] selmodkled,
  output [6:0] catod,
  output finishled,
  output Output_1,
  output stage3,
  output Output_2,
  output Output_3,
  output stage2,
  output stage1,
  output stage0
);

  wire debounce_1_1_o, debouncer_3sec_1_delay_3sec, div1sec_1_clk_1sec, divizor_200hz_1_clk_200hz,
       uc_1_en_fulltime, uc_1_en_st0, uc_1_en_st1, uc_1_en_st2, uc_1_en_st3, uc_1_ftms,
       verficare1modauto_1_just1auto;
  wire [3:0] converter_1_n1, converter_1_n2, converter_1_n3, verficare1modauto_1_mode;
  wire [6:0] decoderauto_1_temp, inel_1_nr, mux_temperature_1_temp, timecalculatormanual_1_outputtemp;
  wire [7:0] codificatorauto_1_informatietm, decoderauto_1_fulltime, decoderauto_1_timestage0,
       decoderauto_1_timestage1, decoderauto_1_timestage2, decoderauto_1_timestage3,
       mux_final_time_1_timpafisor, mux_stage0_time_1_stage0time, mux_stage1_time_1_stage1time,
       mux_stage2_time_1_stage2time, mux_stage3_time_1_stage3time, muxfinaltime2_1_fulltime,
       numaratorcicluspalare_1_timpnumarator, timecalculatormanual_1_fulltime,
       timecalculatormanual_1_stage0_time, timecalculatormanual_1_stage1_time,
       timecalculatormanual_1_stage2_time, timecalculatormanual_1_stage3_time;

  DEBOUNCER_3SEC debouncer_3sec_1 (
    .Button_Start(Start), .CLK_1SEC(div1sec_1_clk_1sec), .Delay_3SEC(debouncer_3sec_1_delay_3sec));
  div1sec div1sec_1 (.CLK_100MHZ(Clk100MHZ), .CLK_1sec(div1sec_1_clk_1sec));
  debounce_1 debounce_1_1 (.BUT(ButonTemp), .CLK_1sec(div1sec_1_clk_1sec), .O(debounce_1_1_o));
  muxfinaltime2 muxfinaltime2_1 (
    .FullTimeAuto(decoderauto_1_fulltime), .FullTimeManual(timecalculatormanual_1_fulltime),
    .Enable_Manual(manualsw), .FullTime(muxfinaltime2_1_fulltime));
  Verficare1ModAuto verficare1modauto_1 (
    .Mod1(Mod1), .Mod2(Mod2), .Mod3(Mod3), .Mod4(Mod4), .clk(Clk100MHZ), .Mode(verficare1modauto_1_mode),
    .Just1Auto(verficare1modauto_1_just1auto));
  Inel inel_1 (.Btn(debounce_1_1_o), .nr(inel_1_nr));
  TimeCalculatorManual timecalculatormanual_1 (
    .PreWash(pwled), .ExtraRinse(erled), .InputTemp(inel_1_nr), .FullTime(timecalculatormanual_1_fulltime),
    .Stage0_Time(timecalculatormanual_1_stage0_time), .Stage1_Time(timecalculatormanual_1_stage1_time),
    .Stage2_Time(timecalculatormanual_1_stage2_time), .Stage3_Time(timecalculatormanual_1_stage3_time),
    .OutputTemp(timecalculatormanual_1_outputtemp));
  CodificatorAuto codificatorauto_1 (
    .En(verficare1modauto_1_just1auto), .Mods(verficare1modauto_1_mode), .Temp(SwitchTemp),
    .InformatieTM(codificatorauto_1_informatietm));
  UC uc_1 (
    .Door(door), .Start_Program(debouncer_3sec_1_delay_3sec), .RESET(rst), .ManualMod(manualsw),
    .PreWash(prewashsw), .ExtraRinse(extrarinsesw), .CLK(Clk100MHZ),
    .ModAuto(codificatorauto_1_informatietm), .DoneStage0(stage0), .DoneStage1(stage1), .DoneStage2(stage2),
    .DoneStage3(stage3), .Temp(mux_temperature_1_temp), .DoorLed(doorled), .Sel_Mod(selmodkled),
    .Sel_PW(pwled), .Sel_XR(erled), .Finish(finishled), .En_St0(uc_1_en_st0), .En_St1(uc_1_en_st1),
    .En_St2(uc_1_en_st2), .En_St3(uc_1_en_st3), .En_FullTime(uc_1_en_fulltime), .Sel50(Output_1),
    .Sel60(Output_2), .Sel75(Output_3), .FTMS(uc_1_ftms));
  DecoderAuto decoderauto_1 (
    .StringCod(codificatorauto_1_informatietm), .TimeStage0(decoderauto_1_timestage0),
    .TimeStage1(decoderauto_1_timestage1), .TimeStage2(decoderauto_1_timestage2),
    .TimeStage3(decoderauto_1_timestage3), .FullTime(decoderauto_1_fulltime), .Temp(decoderauto_1_temp));
  Mux_Temperature mux_temperature_1 (
    .TempAuto(decoderauto_1_temp), .TempManual(timecalculatormanual_1_outputtemp), .Enable_Manual(manualsw),
    .Temp(mux_temperature_1_temp));
  mux_final_time mux_final_time_1 (
    .FullTime(muxfinaltime2_1_fulltime), .TimpNumarator(numaratorcicluspalare_1_timpnumarator),
    .Ok_Button(uc_1_ftms), .TimpAfisor(mux_final_time_1_timpafisor));
  MUX_STAGE3_TIME mux_stage3_time_1 (
    .Stage3Time_Auto(decoderauto_1_timestage3), .Stage3Time_Manual(timecalculatormanual_1_stage3_time),
    .Enable_Manual(manualsw), .Stage3time(mux_stage3_time_1_stage3time));
  MUX_STAGE1_TIME mux_stage1_time_1 (
    .Stage1Time_Auto(decoderauto_1_timestage1), .Stage1Time_Manual(timecalculatormanual_1_stage1_time),
    .Enable_Manual(manualsw), .Stage1time(mux_stage1_time_1_stage1time));
  MUX_STAGE0_TIME mux_stage0_time_1 (
    .Stage0Time_Auto(decoderauto_1_timestage0), .Stage0Time_Manual(timecalculatormanual_1_stage0_time),
    .Enable_Manual(manualsw), .Stage0time(mux_stage0_time_1_stage0time));
  MUX_STAGE2_TIME mux_stage2_time_1 (
    .Stage2Time_Auto(decoderauto_1_timestage2), .Stage2Time_Manual(timecalculatormanual_1_stage2_time),
    .Enable_Manual(manualsw), .Stage2time(mux_stage2_time_1_stage2time));
  NumaratorCicluSpalare numaratorcicluspalare_1 (
    .StartNumarator(uc_1_en_fulltime), .FullTime(muxfinaltime2_1_fulltime), .CLK_1min(div1sec_1_clk_1sec),
    .Reset(rst), .TimpNumarator(numaratorcicluspalare_1_timpnumarator));
  Numarator_stage3 numarator_stage3_1 (
    .Reset(rst), .Enable(uc_1_en_st3), .Time3(mux_stage3_time_1_stage3time), .CLK_1min(div1sec_1_clk_1sec),
    .Done_stage3(stage3));
  Numarator_stage2 numarator_stage2_1 (
    .Reset(rst), .Enable(uc_1_en_st2), .Time2(mux_stage2_time_1_stage2time), .CLK_1min(div1sec_1_clk_1sec),
    .Done_stage2(stage2));
  Numarator_stage1 numarator_stage1_1 (
    .Reset(rst), .Enable(uc_1_en_st1), .Time1(mux_stage1_time_1_stage1time), .CLK_1min(div1sec_1_clk_1sec),
    .Done_stage1(stage1));
  Numarator_stage0 numarator_stage0_1 (
    .RESET(rst), .Enable(uc_1_en_st0), .Time0(mux_stage0_time_1_stage0time), .Clk_1min(div1sec_1_clk_1sec),
    .Done_stage0(stage0));
  converter converter_1 (
    .A(mux_final_time_1_timpafisor), .n1(converter_1_n1), .n2(converter_1_n2), .n3(converter_1_n3));
  Divizor_200HZ divizor_200hz_1 (.CLK_100MHZ(Clk100MHZ), .CLK_200HZ(divizor_200hz_1_clk_200hz));
  ssd ssd_1 (
    .n1(converter_1_n1), .n2(converter_1_n2), .n3(converter_1_n3), .CLK(divizor_200hz_1_clk_200hz),
    .Anod(anod), .Catod(catod));
endmodule

// VHDL entity div1sec, as the project stores it:
--------------------------------------------------------------------------------
-- Project :
-- File    :
-- Autor   : Edi Moga
-- Date    :
--
--------------------------------------------------------------------------------
-- Description :
--
--------------------------------------------------------------------------------

LIBRARY ieee;
USE ieee.std_logic_1164.all;

USE ieee.std_logic_unsigned.all;
ENTITY div1sec IS
  PORT (

	CLK_100MHZ : in std_logic;
	CLK_1sec 		 : out std_logic
    );
END div1sec;

ARCHITECTURE TypeArchitecture OF div1sec IS

signal semnal : std_logic := '0';

BEGIN

process(CLK_100MHZ)

variable num : integer := 0;

begin

		if rising_edge(CLK_100MHZ) then
			num := num + 1;
		
	if num = 50_000_000  then
		num := 0;
		semnal <= not semnal;
		else
		semnal <= semnal;
		end if;
	end if;

end process;

CLK_1sec <= semnal;

END TypeArchitecture;

// VHDL entity divizor1min, as the project stores it:
--------------------------------------------------------------------------------
-- Project :
-- File    :
-- Autor   : Edi Moga
-- Date    :
--
--------------------------------------------------------------------------------
-- Description :
--
--------------------------------------------------------------------------------

LIBRARY ieee;
USE ieee.std_logic_1164.all;

USE ieee.std_logic_unsigned.all;
ENTITY divizor1min IS
  PORT (

 	    CLK_1sec : in std_logic;
 	    RST	   : in std_logic;
 	    CLK_1m   : out std_logic
    );
END divizor1min;



ARCHITECTURE TypeArchitecture OF divizor1min IS

signal semnal : std_logic := '0';

BEGIN
	
	process(CLK_1sec , RST)
	 variable nr : std_logic_vector(4 downto 0) :=(others =>'0');
		begin
			if RST = '1' then
				nr := (others => '0');
				semnal <= '0';
			else
				if falling_edge(CLK_1sec) then
					nr := nr + 1;

				if nr = 30 then
					nr := (others => '0');
					semnal <= not semnal;
				end if;
			end if;
			end if;
			
		end process;


CLK_1m <= semnal;
END TypeArchitecture;

// VHDL entity debounce_1, as the project stores it:
--Autor : Edi Moga



LIBRARY ieee;
USE ieee.std_logic_1164.all;

USE IEEE.STD_LOGIC_UNSIGNED.ALL;
ENTITY debounce_1 IS
  PORT (
 	BUT: in std_logic;
 	CLK_1sec : in std_logic;
 	O   : out std_logic
    );
END debounce_1;


ARCHITECTURE struct OF debounce_1 IS

COMPONENT bistabil IS 
	PORT(
		D: in std_logic;
		CLK  : in std_logic;
		Q  : out std_logic
	);
END COMPONENT;

SIGNAL semnal1 : std_logic;

BEGIN

d1: bistabil port map(BUT , CLK_1sec , semnal1);


O <= semnal1;

END struct;



LIBRARY ieee;
USE ieee.std_logic_1164.all;
USE IEEE.STD_LOGIC_UNSIGNED.ALL;
ENTITY bistabil IS 
	PORT(
		D: in std_logic;
		CLK  : in std_logic;
		Q  : out std_logic
	);
END bistabil;


ARCHITECTURE comp of bistabil is


BEGIN
	PROCESS(CLK)
begin 
	IF rising_edge(CLK) then Q <= D;

	END IF;

	END PROCESS;


END ARCHITECTURE;

// VHDL entity DEBOUNCER_3SEC, as the project stores it:
--------------------------------------------------------------------------------
-- Project :
-- File    :
-- Autor   : Ricu Razvan
-- Date    :
--
--------------------------------------------------------------------------------
-- Description :
--
--------------------------------------------------------------------------------

LIBRARY ieee;
USE ieee.std_logic_1164.all;

ENTITY DEBOUNCER_3SEC IS
  PORT (

	Button_Start : in std_logic;
	CLK_1SEC	   : in std_logic;
	Delay_3SEC   : out std_logic
 	
    );
END DEBOUNCER_3SEC;

--------------------------------------------------------------------------------
--Complete your VHDL description below
--------------------------------------------------------------------------------

ARCHITECTURE TypeArchitecture OF DEBOUNCER_3SEC IS

component bistabil_d IS
  PORT (
 D,clk: in std_logic;
 Q:out std_logic
    );
END component;

component poarta_si is
port(
A,B,C:in std_logic;
D:out std_logic
);
end component;
signal Y1,Y2,Y3:std_logic;
BEGIN

C1:bistabil_d port map(Button_Start,CLK_1SEC,Y1);
C2:bistabil_d port map(Y1,CLK_1SEC,Y2);
C3:bistabil_d port map(Y2,CLK_1SEC,Y3);
C4:poarta_si port map(Y1,Y2,Y3,Delay_3SEC);
END TypeArchitecture;

--- ddddddddddddddddddddddddddddddddddd
LIBRARY ieee;
USE ieee.std_logic_1164.all;
use ieee.std_logic_unsigned.all;

ENTITY bistabil_d IS
  PORT (
 D,clk: in std_logic;
 Q:out std_logic
    );
END bistabil_d;

ARCHITECTURE comport OF bistabil_d IS

BEGIN

process(clk)
begin 
if rising_edge(clk) then
	Q<=D;
end if;
end process;
END comport;

---poartsiiiiiiiiiiiiiiiiiiiiiiiiiiiiiiiiiiiiii
LIBRARY ieee;
USE ieee.std_logic_1164.all;
use ieee.std_logic_unsigned.all;

ENTITY poarta_si IS
  PORT (
	A,B,C: in std_logic;
 D: out std_logic
    );
END poarta_si;

ARCHITECTURE fluxdedate OF poarta_si IS

BEGIN
D<=A and B and C;

END fluxdedate;

// VHDL entity ssd, as the project stores it:
-------------------------------------------------------------------------------


--Autor : Edi Moga

LIBRARY ieee;
USE ieee.std_logic_1164.all;

USE ieee.std_logic_unsigned.all;

USE ieee.numeric_std.all;
ENTITY ssd IS
  PORT (
  	n1 : in std_logic_vector (3 downto 0);
  	n2 : in std_logic_vector (3 downto 0);
  	n3 : in std_logic_vector (3 downto 0);
  	CLK :  in std_logic;
  	Anod : out std_logic_vector (3 downto 0);
  	Catod : out std_logic_vector (6 downto 0)

  	--pozitie : out std_logic_vector (2 downto 0)
  
    );
END ssd;


ARCHITECTURE TypeArchitecture OF ssd IS

signal cat : std_logic_vector (6 downto 0) := "0000000";
signal ano : std_logic_vector (3 downto 0) := "0000";

signal poz : std_logic_vector (2 downto 0) := "000";

signal digit : std_logic_vector (3 downto 0) := "0000";


BEGIN

	process(CLK)

	begin
		if rising_edge(CLK) then
			poz <= poz +1;
		end if;
			

	end process;

	process(poz)	
		begin

			case poz is
				--when "00" =>
					--ano <= "1000";

				--when "01" =>
				--	ano <= "0100";

				when "001" =>
					ano <= "0100";
					digit <= n3;
				when "010" =>
					ano <= "0010";
					digit <= n2 ;
				when "011" =>
					ano <= "0001";
					digit <= n1;
				when others =>
					ano <= "0000";
					digit <= "1111";
				end case;

		end process;

	process(digit)
		begin

			case digit is
				when "0000" =>
					cat <= "0111111";
				when x"1" =>
					cat <= "0000110";
				when x"2" =>
					cat <= "1011011";
				when x"3" =>
					cat <= "1001111";
				when x"4" =>
					cat <= "1100110";
				when x"5" =>
					cat <= "1101101";
				when x"6" =>
					cat <= "1111101";
				when x"7" =>
					cat <= "0100111";
				when x"8" =>
					cat <= "1111111";
				when x"9" =>
					cat <= "1101111";
				when others =>
					cat <= "0000000";

			end case;

		end process;

	Anod <= ano ;
	Catod <= cat;
	--pozitie <= poz;

END TypeArchitecture;

// VHDL entity Divizor_200HZ, as the project stores it:
--------------------------------------------------------------------------------
-- Project :
-- File    :
-- Autor   : Edi Moga
-- Date    :
--
--------------------------------------------------------------------------------
-- Description :
--
--------------------------------------------------------------------------------

LIBRARY ieee;
USE ieee.std_logic_1164.all;

USE ieee.std_logic_unsigned.all;

ENTITY Divizor_200HZ IS
  PORT (
	CLK_100MHZ : in std_LOGIC;
	CLK_200HZ	 : out std_logic
    );
END Divizor_200HZ;



ARCHITECTURE TypeArchitecture OF Divizor_200HZ IS

signal semnal : std_logic := '0';

BEGIN

	process(CLK_100MHZ)
	variable aux : integer := 0;
		begin

			if rising_edge(CLK_100MHZ) then
				aux := aux + 1;
				
				if aux = 100000 then
					aux := 0;
					semnal <= not semnal;
				else 
					semnal <= semnal;
				end if;
			end if;

		end process;

	
CLK_200HZ <= semnal;



END TypeArchitecture;

// VHDL entity TimeCalculatorManual, as the project stores it:
--------------------------------------------------------------------------------
-- Project :
-- File    :
-- Autor   : Ricu Razvan
-- Date    :
--
--------------------------------------------------------------------------------
-- Description :
--
--------------------------------------------------------------------------------

LIBRARY ieee;
USE ieee.std_logic_1164.all;
USE ieee.std_logic_unsigned.all;
use ieee.numeric_std.all;
ENTITY TimeCalculatorManual IS
  PORT (
 	
	PreWash	 : in std_logic;
	ExtraRinse : in std_logic;
	InputTemp : in std_logic_vector (6 downto 0);
	FullTime  : out std_logic_vector (7 downto 0);
	Stage0_Time : out std_logic_vector (7 downto 0);
	Stage1_Time : out std_logic_vector (7 downto 0);
	Stage2_Time : out std_logic_vector (7 downto 0);
	Stage3_Time : out std_logic_vector (7 downto 0);
	
	OutputTemp : out std_logic_vector (6 downto 0)
    );
END TimeCalculatorManual;

--------------------------------------------------------------------------------
--Complete your VHDL description below
--------------------------------------------------------------------------------

ARCHITECTURE TypeArchitecture OF TimeCalculatorManual IS

BEGIN
			
process(PreWash,ExtraRinse,InputTemp)
variable Time0:std_logic_vector(7 downto 0):=(others=>'0');
variable Time1:std_logic_vector(7 downto 0):=(others=>'0');
variable Time2:std_logic_vector(7 downto 0):=(others=>'0');
variable Time3:std_logic_vector(7 downto 0):=(others=>'0');
variable Var0:integer:=0;
variable Var1:integer:=0;
variable Var2:integer:=0;
variable Var3:integer:=0;
variable Var4:integer:=0;
variable Var5:integer:=0;
variable FullTimevar:std_logic_vector(7 downto 0):=(others=>'0');
variable Temp:std_logic_vector(6 downto 0):=(others=>'0');
begin 

Var5:=to_integer(unsigned(InputTemp));
	Temp:=std_logic_vector(to_unsigned(Var5,Temp'length));
			Var3:=28;
			if Var5=50 then Var1:=24;
			end if;
			if Var5=60 then Var1:=34;
			end if;
			if Var5=75 then Var1:=49;
			end if;
			
			if PreWash='1' then Var0:=14;
			else  Var0:=4;
			end if;
			if ExtraRinse='1' then Var2:=10;
			else Var2:=5;
			end if;
			
			
			Time0:=std_logic_vector(to_unsigned(Var0,Time0'length));
			Time1:=std_logic_vector(to_unsigned(Var1,Time1'length));
			Time2:=std_logic_vector(to_unsigned(Var2,Time2'length));
			Time3:=std_logic_vector(to_unsigned(Var3,Time3'length));
		
			var4 := var0+var1+var2+var3;
			FullTimeVar:=std_logic_vector(to_unsigned(Var4,FullTimevar'length));
		Stage0_Time<=Time0;
Stage1_Time<=Time1;
Stage2_Time<=Time2;
Stage3_Time<=Time3;
FullTime<=FullTimevar;
OutputTemp<=Temp;
end process;



END TypeArchitecture;

// VHDL entity Verficare1ModAuto, as the project stores it:
--------------------------------------------------------------------------------
-- Project :
-- File    :
-- Autor   : Ricu Razvan
-- Date    :
--
--------------------------------------------------------------------------------
-- Description :
--
--------------------------------------------------------------------------------

LIBRARY ieee;
USE ieee.std_logic_1164.all;

ENTITY Verficare1ModAuto IS
  PORT (
 	Mod1 : in std_logic;
 	Mod2: in std_logic;
 	Mod3 : in std_logic;
 	Mod4 : in std_logic;
 	clk: in std_logic;
	Mode:out std_logic_vector(3 downto 0);
 	Just1Auto : out std_logic
 	
    );
END Verficare1ModAuto;

--------------------------------------------------------------------------------
--Complete your VHDL description below
--------------------------------------------------------------------------------

ARCHITECTURE TypeArchitecture OF Verficare1ModAuto IS

BEGIN
process(clk)
begin
if Mod1='0' then
if Mod2='0' then
if Mod3='0' then
if Mod4='0' then Just1Auto<='0'; Mode<="0000";
end if;
end if;
end if;
end if;
if Mod1='1' then Just1Auto<='1'; Mode<="0001";
	if Mod2 ='1' then Just1Auto<='0'; Mode<="0000";
	end if;
	if Mod3 ='1' then Just1Auto<='0'; Mode<="0000";
	end if;
	if Mod4 ='1' then Just1Auto<='0'; Mode<="0000";
	end if;
end if;
if Mod2='1' then Just1Auto<='1'; Mode<="0010";
	if Mod1 ='1' then Just1Auto<='0'; Mode<="0000";
	end if;
	if Mod3 ='1' then Just1Auto<='0'; Mode<="0000";
	end if;
	if Mod4 ='1' then Just1Auto<='0'; Mode<="0000";
	end if;
end if;
if Mod3='1' then Just1Auto<='1'; Mode<="0100";
	if Mod1 ='1' then Just1Auto<='0'; Mode<="0000";
	end if;
	if Mod2 ='1' then Just1Auto<='0'; Mode<="0000";
	end if;
	if Mod4 ='1' then Just1Auto<='0'; Mode<="0000";
	end if;
end if;
if Mod4='1' then Just1Auto<='1'; Mode<="1000";
	if Mod1 ='1' then Just1Auto<='0'; Mode<="0000";
	end if;
	if Mod2 ='1' then Just1Auto<='0'; Mode<="0000";
	end if;
	if Mod3 ='1' then Just1Auto<='0'; Mode<="0000";
	end if;
end if;
end process;
END TypeArchitecture;

// VHDL entity Inel, as the project stores it:
--------------------------------------------------------------------------------
-- Project :
-- File    :
-- Autor   : Edi Moga
-- Date    :
--
--------------------------------------------------------------------------------
-- Description :
--
--------------------------------------------------------------------------------

LIBRARY ieee;
USE ieee.std_logic_1164.all;

USE ieee.std_logic_unsigned.all;

ENTITY Inel IS
  PORT (
 	Btn : in std_logic ;
 	nr : out std_logic_vector (6 downto 0)
    );
END Inel;



ARCHITECTURE TypeArchitecture OF Inel IS
signal test : std_logic_vector (6 downto 0) := (others => '0');
signal testbit : std_logic_vector (6 downto 0) := (others => '0');

signal poz : std_logic_vector (2 downto 0) := "000";


BEGIN

	process(Btn)
		begin
			if falling_edge(Btn) then
			poz <= poz + 1; 
	
			if poz = x"3" then 
				poz <= "001";
			end if;
			
		end if;
		end process;

process(poz)
	variable l : std_logic_vector (6 downto 0) := (others => '0');
		begin


			
			
			case poz is
				when "001" =>  l:= "0110010"; 
				when "010" => l:= "0111100"; 
				when "011" =>  l:= "1001011"; 
				when others =>l:= "0000000"; 
			end case;	

		testbit <= l;
		
		end process;

nr <= testbit;
END TypeArchitecture;

// VHDL entity NumaratorCicluSpalare, as the project stores it:
--------------------------------------------------------------------------------
-- Project :
-- File    :
-- Autor   : Moga Eduard/Ricu Razvan
-- Date    :
--
--------------------------------------------------------------------------------
-- Description :
--
--------------------------------------------------------------------------------

LIBRARY ieee;
USE ieee.std_logic_1164.all;

USE ieee.std_logic_unsigned.all;

ENTITY NumaratorCicluSpalare IS
  PORT (
  	StartNumarator : in std_logic;
 	FullTime : in std_logic_vector (7 downto 0);
 	CLK_1min : in std_logic;
 	Reset	    : in std_logic;
	TimpNumarator : out std_logic_vector (7 downto 0)
    );
END NumaratorCicluSpalare;

--------------------------------------------------------------------------------
--Complete your VHDL description below
--------------------------------------------------------------------------------

ARCHITECTURE TypeArchitecture OF NumaratorCicluSpalare IS

signal don : std_logic := '0';
signal stop_time : std_logic_vector(7 downto 0) := "ZZZZZZZZ";
signal stop : std_logic := '0';
BEGIN

	stop_time <= FullTime;

	process(Clk_1min,Reset, StartNumarator)
	
		variable t : std_logic_vector (7 downto 0) := "ZZZZZZZZ";
		variable ok : std_logic := '0';
		variable fct : std_logic := '0';
		begin
	if Reset = '1' then 
				don<='0';
				ok:='0';
				stop <= '0';
				
	else
		if stop = '0' then	
			
			if StartNumarator = '0' then
				t := t;

			else 
				if falling_edge(Clk_1min) then
		
					if ok = '0' then
						ok := '1';
						t := FullTime;
					else
						t := t - 1;
					end if;
					if  t = "00000000" then
						don <= '1' ;
						t := t;
						stop <= '1';
					
					end if;	
				end if;	
			end if;

		else
			t := t;
		end if;
		
	end if;
		--don <=  fct;
		TimpNumarator<=t;
		end process;	
END TypeArchitecture;

// VHDL entity MUX_STAGE1_TIME, as the project stores it:
--------------------------------------------------------------------------------
-- Project :
-- File    :
-- Autor   : Ricu Razvan
-- Date    :
--
--------------------------------------------------------------------------------
-- Description :
--
--------------------------------------------------------------------------------

LIBRARY ieee;
USE ieee.std_logic_1164.all;

ENTITY MUX_STAGE1_TIME IS
  PORT (
   
  Stage1Time_Auto:in std_logic_vector(7 downto 0);
   Stage1Time_Manual:in std_logic_vector(7 downto 0);
    Enable_Manual: in std_logic;
    Stage1time: out std_logic_vector(7 downto 0)
    );
END MUX_STAGE1_TIME;

--------------------------------------------------------------------------------
--Complete your VHDL description below
--------------------------------------------------------------------------------

ARCHITECTURE TypeArchitecture OF MUX_STAGE1_TIME IS

signal  t1 : std_logic_vector (7 downto 0) := "00000000";




BEGIN

	with Enable_Manual select Stage1time <=
	Stage1Time_Manual when '1',
	Stage1Time_Auto when '0',
	"00000000" when others; 
	
END TypeArchitecture;

// VHDL entity MUX_STAGE2_TIME, as the project stores it:
--------------------------------------------------------------------------------
-- Project :
-- File    :
-- Autor   : Ricu Razvan
-- Date    :
--
--------------------------------------------------------------------------------
-- Description :
--
--------------------------------------------------------------------------------

LIBRARY ieee;
USE ieee.std_logic_1164.all;

ENTITY MUX_STAGE2_TIME IS
  PORT (
  Stage2Time_Auto:in std_logic_vector(7 downto 0);
    Stage2Time_Manual:in std_logic_vector(7 downto 0);
    Enable_Manual: in std_logic;
    Stage2time: out std_logic_vector(7 downto 0)
    );
END MUX_STAGE2_TIME;

--------------------------------------------------------------------------------
--Complete your VHDL description below
--------------------------------------------------------------------------------

ARCHITECTURE TypeArchitecture OF MUX_STAGE2_TIME IS

signal  t1 : std_logic_vector (7 downto 0) := "00000000";

BEGIN

	with Enable_Manual select Stage2time <=
	Stage2Time_Manual when '1',
	Stage2Time_Auto when '0',
	"00000000" when others; 
END TypeArchitecture;

// VHDL entity MUX_STAGE3_TIME, as the project stores it:
--------------------------------------------------------------------------------
-- Project :
-- File    :
-- Autor   :Ricu Razvan
-- Date    :
--
--------------------------------------------------------------------------------
-- Description :
--
--------------------------------------------------------------------------------

LIBRARY ieee;
USE ieee.std_logic_1164.all;

ENTITY MUX_STAGE3_TIME IS
  PORT (
  Stage3Time_Auto:in std_logic_vector(7 downto 0);
    Stage3Time_Manual:in std_logic_vector(7 downto 0);
    Enable_Manual: in std_logic;
    Stage3time: out std_logic_vector(7 downto 0)
    );
END MUX_STAGE3_TIME;

--------------------------------------------------------------------------------
--Complete your VHDL description below
--------------------------------------------------------------------------------

ARCHITECTURE TypeArchitecture OF MUX_STAGE3_TIME IS

signal  t1 : std_logic_vector (7 downto 0) := "00000000";
BEGIN
	with Enable_Manual select Stage3time <=
	Stage3Time_Manual when '1',
	Stage3Time_Auto when '0',
	"00000000" when others; 
END TypeArchitecture;

// VHDL entity Numarator_stage1, as the project stores it:
--------------------------------------------------------------------------------
-- Project :
-- File    :
-- Autor   :Ricu Razvan/Moga Eduard
-- Date    :
--
--------------------------------------------------------------------------------
-- Description :
--
--------------------------------------------------------------------------------

LIBRARY ieee;
USE ieee.std_logic_1164.all;
USE ieee.std_logic_unsigned.all;

ENTITY Numarator_stage1 IS
  PORT (
  	Reset : in std_logic;
  	Enable : in std_logic;
 	Time1 : in std_logic_vector (7 downto 0);
 	CLK_1min : in std_logic;
 	Done_stage1: out std_logic

    );
END Numarator_stage1;

--------------------------------------------------------------------------------
--Complete your VHDL description below
--------------------------------------------------------------------------------

ARCHITECTURE TypeArchitecture OF Numarator_stage1 IS

signal aux : std_logic_vector (7 downto 0) := "11111111";



signal don : std_logic := '0';
signal stop_time : std_logic_vector(7 downto 0) := "11111111";
signal stop : std_logic := '0';
BEGIN

	stop_time <= Time1;

	process(Clk_1min,Reset, enable)
	
		variable t : std_logic_vector (7 downto 0) := "11111111";
		variable ok : std_logic := '0';
		variable fct : std_logic := '0';
		begin
	if Reset = '1' then 
				don<='0';
				ok:='0';
				stop <= '0';
				
	else
		if stop = '0' then	
			
			if Enable = '0' then
				t := t;

			else 
				if falling_edge(Clk_1min) then
		
					if ok = '0' then
						ok := '1';
						t := Time1;
					else
						t := t - 1;
					end if;
					if  t = "00000000" then
						don <= '1' ;
						t := t;
						stop <= '1';
					
					end if;	
				end if;	
			end if;

		else
			t := t;
		end if;
		
	end if;
		--don <=  fct;
		end process;	


Done_stage1 <= don;
END TypeArchitecture;

// VHDL entity Numarator_stage2, as the project stores it:
--------------------------------------------------------------------------------
-- Project :
-- File    :
-- Autor   :  Ricu Razvan/Moga Eduard
-- Date    :
--
--------------------------------------------------------------------------------
-- Description :
--
--------------------------------------------------------------------------------

LIBRARY ieee;
USE ieee.std_logic_1164.all;
USE ieee.std_logic_unsigned.all;


ENTITY Numarator_stage2 IS
  PORT (
  Reset : in std_logic;
  Enable : in std_logic;
 	Time2 : in std_logic_vector (7 downto 0);
 	CLK_1min : in std_logic;
 	Done_stage2: out std_logic
    );
END Numarator_stage2;

--------------------------------------------------------------------------------
--Complete your VHDL description below
--------------------------------------------------------------------------------

ARCHITECTURE TypeArchitecture OF Numarator_stage2 IS


signal aux : std_logic_vector (7 downto 0) := "11111111";



signal don : std_logic := '0';
signal stop_time : std_logic_vector(7 downto 0) := "11111111";
signal stop : std_logic := '0';
BEGIN

	stop_time <= Time2;

	process(Clk_1min,Reset, enable)
	
		variable t : std_logic_vector (7 downto 0) := "11111111";
		variable ok : std_logic := '0';
		variable fct : std_logic := '0';
		begin
	if Reset = '1' then 
				don<='0';
				ok:='0';
				stop <= '0';
				
	else
		if stop = '0' then	
			
			if Enable = '0' then
				t := t;

			else 
				if falling_edge(Clk_1min) then
		
					if ok = '0' then
						ok := '1';
						t := Time2;
					else
						t := t - 1;
					end if;
					if  t = "00000000" then
						don <= '1' ;
						t := t;
						stop <= '1';
					
					end if;	
				end if;	
			end if;

		else
			t := t;
		end if;
		
	end if;
		--don <=  fct;
		end process;	


Done_stage2 <= don;

END TypeArchitecture;

// VHDL entity Numarator_stage3, as the project stores it:
--------------------------------------------------------------------------------
-- Project :
-- File    :
-- Autor   :  Ricu Razvan/Moga Eduard
-- Date    :
--
--------------------------------------------------------------------------------
-- Description :
--
--------------------------------------------------------------------------------

LIBRARY ieee;
USE ieee.std_logic_1164.all;
USE ieee.std_logic_unsigned.all;

ENTITY Numarator_stage3 IS
  PORT (
 	Reset : in std_logic;
   Enable: in std_logic;
 	Time3 : in std_logic_vector (7 downto 0);
 	CLK_1min : in std_logic;
 	Done_stage3: out std_logic
    );
END Numarator_stage3;

--------------------------------------------------------------------------------
--Complete your VHDL description below
--------------------------------------------------------------------------------

ARCHITECTURE TypeArchitecture OF Numarator_stage3 IS


signal aux : std_logic_vector (7 downto 0) := "11111111";



signal don : std_logic := '0';
signal stop_time : std_logic_vector(7 downto 0) := "11111111";
signal stop : std_logic := '0';
BEGIN

	stop_time <= Time3;

	process(Clk_1min,Reset, enable)
	
		variable t : std_logic_vector (7 downto 0) := "11111111";
		variable ok : std_logic := '0';
		variable fct : std_logic := '0';
		begin
	if Reset = '1' then 
				don<='0';
				ok:='0';
				stop <= '0';
				
	else
		if stop = '0' then	
			
			if Enable = '0' then
				t := t;

			else 
				if falling_edge(Clk_1min) then
		
					if ok = '0' then
						ok := '1';
						t := Time3;
					else
						t := t - 1;
					end if;
					if  t = "00000000" then
						don <= '1' ;
						t := t;
						stop <= '1';
					
					end if;	
				end if;	
			end if;

		else
			t := t;
		end if;
		
	end if;
		--don <=  fct;
		end process;	


Done_stage3 <= don;
END TypeArchitecture;

// VHDL entity Numarator_stage0, as the project stores it:
--------------------------------------------------------------------------------
-- Project :
-- File    :
-- Autor   :Ricu Razvan/Moga Eduard
-- Date    :
--
--------------------------------------------------------------------------------
-- Description :
--
--------------------------------------------------------------------------------

LIBRARY ieee;
USE ieee.std_logic_1164.all;

USE ieee.std_logic_unsigned.all;

ENTITY Numarator_stage0 IS
  PORT (
  	RESET    : in std_logic;
	Enable   : in std_logic;
	Time0 : in std_logic_vector (7 downto 0);
	Clk_1min  : in std_logic;

	Done_stage0 : out std_logic 
 	
    );
END Numarator_stage0;


ARCHITECTURE TypeArchitecture OF Numarator_stage0 IS

signal aux : std_logic_vector (7 downto 0) := "11111111";



signal don : std_logic := '0';
signal stop_time : std_logic_vector(7 downto 0) := "11111111";
signal stop : std_logic := '0';
BEGIN

	stop_time <= Time0;

	process(Clk_1min,Reset, enable)
	
		variable t : std_logic_vector (7 downto 0) := "11111111";
		variable ok : std_logic := '0';
		variable fct : std_logic := '0';
		begin
	if Reset = '1' then 
				don<='0';
				ok:='0';
				stop <= '0';
				
	else
		if stop = '0' then	
			
			if Enable = '0' then
				t := t;

			else 
				if falling_edge(Clk_1min) then
		
					if ok = '0' then
						ok := '1';
						t := Time0;
					else
						t := t - 1;
					end if;
					if  t = "00000000" then
						don <= '1' ;
						t := t;
						stop <= '1';
					
					end if;	
				end if;	
			end if;

		else
			t := t;
		end if;
		
	end if;
		--don <=  fct;
		end process;	


Done_stage0 <= don;

END TypeArchitecture;

// VHDL entity divizor4se, as the project stores it:
--------------------------------------------------------------------------------
-- Project :
-- File    :
-- Autor   : Moga Eduard
-- Date    :
--
--------------------------------------------------------------------------------
-- Description :
--
--------------------------------------------------------------------------------

LIBRARY ieee;
USE ieee.std_logic_1164.all;

USE ieee.std_logic_unsigned.all;

ENTITY divizor4se IS
  PORT (
  	CLK_1sec : in std_logic;
  	RST	    : in std_logic;
  	CLK_4sec : out std_logic
    );
END divizor4se;



ARCHITECTURE TypeArchitecture OF divizor4se IS

signal semnal : std_logic := '0';
BEGIN

	process(CLK_1sec)
	variable nr : integer := 0;
		begin

		if RST = '1' then
			nr := 0 ;
			semnal <= '0';
		else
			if falling_edge(CLK_1sec) then
				nr := nr + 1;

			if nr = 2 then
				nr := 0 ;
				semnal <= not semnal;
			else 
				semnal <= semnal;
				
			end if;
		end if;
		end if;
end process;

CLK_4sec <= semnal;

END TypeArchitecture;

// VHDL entity UC, as the project stores it:
--------------------------------------------------------------------------------
-- Project :
-- File    :
-- Autor   : Ricu Razvan/Moga Eduard
-- Date    :
--
--------------------------------------------------------------------------------
-- Description :
--
--------------------------------------------------------------------------------

LIBRARY ieee;
USE ieee.std_logic_1164.all;

ENTITY UC IS
  PORT (
  		Door : in std_logic;
  		Start_Program : in std_logic;
  		RESET : in std_logic;
  		ManualMod : in std_logic;
  		PreWash	: in std_logic;
  		ExtraRinse : in std_logic;
  		CLK 		 : in std_logic;
		------------------------------------------------- Intrari utilizator
  		ModAuto 	: in std_logic_vector(7 downto 0);
  		DoneStage0 : in std_logic;
  		DoneStage1 : in std_logic;
  		DoneStage2 : in std_logic;
  		DoneStage3 : in std_logic;
  		
  		Temp			: in std_logic_vector (6 downto 0);
  		-------------------------------------------------- Intrari de la resurse 
		DoorLed 		: out std_logic;
		Sel_Mod		: out std_logic_vector (4 downto 0);
		Sel_PW		: out std_logic;
		Sel_XR		: out std_logic;
		Finish		: out std_logic;
		En_St0		: out std_logic;
		En_St1		: out std_logic;
		En_St2		: out std_logic;
		En_St3		: out std_logic;
		En_FullTime	: out std_logic;
		Sel50		: out std_logic;
		Sel60 		: out std_logic;
		Sel75 		: out std_logic;
		FTMS			: out std_logic				-- final time mux selector
  		
    );
END UC;




ARCHITECTURE TypeArchitecture OF UC IS

type STAGIU is (A_Init , B0_Manual , B1_Auto , C_Door , E_Start , F0_St0 , F1_St0 , G0_St1 , G1_St1 , H0_St2 , H1_St2 , I0_St3 , I1_St3 , J_Done);

signal St , NextSt : STAGIU;


BEGIN


UPDATE : process(CLK, RESET)
			begin

				if RESET = '1' then 
					St <= A_Init;
				elsif rising_edge(CLK) then
					St <= NextSt;
				end if;
				
		
			end process UPDATE;

TRANZITIE : process(St,Door,Start_Program, ManualMod , ModAuto,DoneStage0, DoneStage1, DoneStage2 , DoneStage3,Reset)
			begin

				case St is 
				when A_Init => if ManualMod = '1' then
								NextSt <= B0_Manual;
							else
								NextSt <= B1_Auto;
							end if;
				when B0_Manual => 	NextSt <= C_Door;

				when B1_Auto   => NextSt   <= C_Door;

				when C_Door =>  if Door = '0' then 
								NextSt <=  A_Init;
							  else
							  	NextSt <=  E_Start;
							  end if;

				when E_Start => if Start_Program = '0' then
								NextSt <= C_Door;
							else
								NextSt <= F0_St0;
							end if;

				when F0_St0 => if Door ='1' then
				
								if DoneStage0 = '1' then
									NextSt <= G0_St1;
								else
									NextSt <= F0_St0;
								end if;
							else
							
								NextSt <= F1_St0;
							end if;
							

				when F1_St0 => if Door = '1' then 
								NextSt <= F0_St0;
							else
								NextSt <= F1_St0;
							end if;


				when G0_St1 => if Door ='1' then
				
								if DoneStage1 = '1' then
									NextSt <= H0_St2;
								else
									NextSt <= G0_St1;
								end if;
							else
						
								NextSt <= G1_St1;
							end if;

				when G1_St1 => if Door = '1' then 
							NextSt <= G0_St1;
						else
							NextSt <= G1_St1;
						end if;


				when H0_St2  => if Door ='1' then
				
								if DoneStage2 = '1' then
									NextSt <= I0_St3;
								else
									NextSt <= H0_St2;
								end if;
							else
							
								NextSt <= H1_St2;
							end if;

				when H1_St2 => if Door = '1' then 
							NextSt <= H0_St2;
						else
							NextSt <= H1_St2;
						end if;



				when I0_St3  => if Door ='1' then
				
								if ModAuto = "00000001" then
									NextSt <= J_Done;
								else
									if DoneStage3 = '1' then
										NextSt <= J_Done;
									else
										NextSt <= I0_St3;
									end if;
								end if;
							else
							
								NextSt <= I1_St3;
							end if;

				when I1_St3 => if Door = '1' then 
							NextSt <= I0_St3;
						else
							NextSt <= I1_St3;
						end if;


				when J_Done => if Door = '1' then
								NextSt <= J_Done;
							else
								NextSt <= A_Init;
							end if;

						
				end case;


			end process TRANZITIE;

Iesire :  process(St,Temp,ModAuto,Door,DoneStage0,DoneStage1,DoneStage2,DoneStage3)
			begin
				Sel_Mod <= "00000";
				Sel_Pw <= '0';
				Sel_XR <= '0';
				Finish <= '0';
				En_St0 <= '0';
				En_St1 <= '0';
				En_St2 <= '0';
				En_St3 <= '0';
				En_FullTime <= '0';
		
				Sel50 <= '0';
				Sel60 <= '0';
				Sel75 <= '0';
				
				FTMS <= '0';
				DoorLed <= '0';

				case St is

				when A_Init => 	
				Sel_Mod <= "00000";
				Sel_Pw <= '0';
				Sel_XR <= '0';
				Finish <= '0';
				En_St0 <= '0';
				En_St1 <= '0';
				En_St2 <= '0';
				En_St3 <= '0';
				En_FullTime <= '0';
		
				Sel50 <= '0';
				Sel60 <= '0';
				Sel75 <= '0';
				
				FTMS <= '0';
				DoorLed <= '0';

				
				when B0_Manual =>  FTMS <= '0';
								Sel_PW <= PreWash;
							    Sel_XR <= ExtraRinse;
							   
							 
							    Sel_Mod <= "10000";
							    if Temp = "0110010" then 
							    Sel50 <= '1'; Sel60 <= '0' ; Sel75 <= '0';
							    elsif Temp = "0111100" then
							    Sel50 <= '0'; Sel60 <= '1' ; Sel75 <= '0';	
							    elsif Temp = "1001011" then
							    Sel50 <= '0'; Sel60 <= '0' ; Sel75 <= '1';
							    end if;
							    
				when B1_Auto =>FTMS <= '0';    
				if ModAuto = "00000001" then
							    Sel_Mod <= "01000";
							    Sel75 <= '1';
							    
							    
							    elsif ModAuto = "00000010" then
							    Sel_Mod <="00100";
							    Sel_PW <='1';
							    Sel60 <='1';
							   

							    elsif ModAuto = "00000100" then
							    Sel_Mod <= "00010";
							    Sel_PW <= '1';
							    Sel_XR <= '1';
							    Sel75 <= '1';
							  

							    elsif ModAuto = "00011000" then
							    Sel_Mod <="00001";
							    Sel_XR <= '1';
							    Sel50 <='1';
							    
							    elsif ModAuto = "00101000" then
							    Sel_Mod <= "00001";
							    Sel_XR <= '1';
							    Sel60 <= '1';
							   
							    elsif ModAuto = "01001000" then
							    Sel_Mod <= "00001";
							    Sel_XR <= '1';
							    Sel75 <= '1';
							  
							    else
							    Sel_Mod <= "00000";
							    Sel_XR <= '0';
							    Sel_PW <= '0';
							    Sel50 <= '0';
							    Sel60 <= '0';
							    Sel75 <= '0';
							   
							    end if;
							    
					when C_DOOR =>FTMS <= '0'; 
					if Door = '1' then
									DoorLed <= '1';
									
								else 
									DoorLed <= '0';
																			
								end if;

					when E_Start =>  FTMS<='0';
					 if ModAuto = "00000001" then
							    Sel_Mod <= "01000";
							    Sel75 <= '1';
							    
							    
							    elsif ModAuto = "00000010" then
							    Sel_Mod <="00100";
							    Sel_PW <='1';
							    Sel60 <='1';
							   

							    elsif ModAuto = "00000100" then
							    Sel_Mod <= "00010";
							    Sel_PW <= '1';
							    Sel_XR <= '1';
							    Sel75 <= '1';
							  

							    elsif ModAuto = "00011000" then
							    Sel_Mod <="00001";
							    Sel_XR <= '1';
							    Sel50 <='1';
							    
							    elsif ModAuto = "00101000" then
							    Sel_Mod <= "00001";
							    Sel_XR <= '1';
							    Sel60 <= '1';
							   
							    elsif ModAuto = "01001000" then
							    Sel_Mod <= "00001";
							    Sel_XR <= '1';
							    Sel75 <= '1';
							  
						
							   else
							   Sel_PW <= PreWash;
							    Sel_XR <= ExtraRinse;
							   
							 
							    Sel_Mod <= "10000";
							    if Temp = "0110010" then 
							    Sel50 <= '1'; Sel60 <= '0' ; Sel75 <= '0';
							    elsif Temp = "0111100" then
							    Sel50 <= '0'; Sel60 <= '1' ; Sel75 <= '0';	
							    elsif Temp = "1001011" then
							    Sel50 <= '0'; Sel60 <= '0' ; Sel75 <= '1';
							    end if;
							    end if;


					when F0_St0 =>  FTMS<='1';En_FullTime<='1';DoorLed<='1';En_St0<='1';
				
					 if ModAuto = "00000001" then
							    Sel_Mod <= "01000";
							    Sel75 <= '1';
							    
							    
							    elsif ModAuto = "00000010" then
							    Sel_Mod <="00100";
							    Sel_PW <='1';
							    Sel60 <='1';
							   

							    elsif ModAuto = "00000100" then
							    Sel_Mod <= "00010";
							    Sel_PW <= '1';
							    Sel_XR <= '1';
							    Sel75 <= '1';
							  

							    elsif ModAuto = "00011000" then
							    Sel_Mod <="00001";
							    Sel_XR <= '1';
							    Sel50 <='1';
							    
							    elsif ModAuto = "00101000" then
							    Sel_Mod <= "00001";
							    Sel_XR <= '1';
							    Sel60 <= '1';
							   
							    elsif ModAuto = "01001000" then
							    Sel_Mod <= "00001";
							    Sel_XR <= '1';
							    Sel75 <= '1';
							  
						
							   else
							   Sel_PW <= PreWash;
							    Sel_XR <= ExtraRinse;
							   
							 
							    Sel_Mod <= "10000";
							    if Temp = "0110010" then 
							    Sel50 <= '1'; Sel60 <= '0' ; Sel75 <= '0';
							    elsif Temp = "0111100" then
							    Sel50 <= '0'; Sel60 <= '1' ; Sel75 <= '0';	
							    elsif Temp = "1001011" then
							    Sel50 <= '0'; Sel60 <= '0' ; Sel75 <= '1';
							    end if;
							    end if;
					
								 
					when F1_St0 =>	
					
					 if ModAuto = "00000001" then
							    Sel_Mod <= "01000";
							    Sel75 <= '1';
							    
							    
							    elsif ModAuto = "00000010" then
							    Sel_Mod <="00100";
							    Sel_PW <='1';
							    Sel60 <='1';
							   

							    elsif ModAuto = "00000100" then
							    Sel_Mod <= "00010";
							    Sel_PW <= '1';
							    Sel_XR <= '1';
							    Sel75 <= '1';
							  

							    elsif ModAuto = "00011000" then
							    Sel_Mod <="00001";
							    Sel_XR <= '1';
							    Sel50 <='1';
							    
							    elsif ModAuto = "00101000" then
							    Sel_Mod <= "00001";
							    Sel_XR <= '1';
							    Sel60 <= '1';
							   
							    elsif ModAuto = "01001000" then
							    Sel_Mod <= "00001";
							    Sel_XR <= '1';
							    Sel75 <= '1';
							  
						 else
							   Sel_PW <= PreWash;
							    Sel_XR <= ExtraRinse;
							   
							 
							    Sel_Mod <= "10000";
							    if Temp = "0110010" then 
							    Sel50 <= '1'; Sel60 <= '0' ; Sel75 <= '0';
							    elsif Temp = "0111100" then
							    Sel50 <= '0'; Sel60 <= '1' ; Sel75 <= '0';	
							    elsif Temp = "1001011" then
							    Sel50 <= '0'; Sel60 <= '0' ; Sel75 <= '1';
							    end if;
							   
							    end if;
							    En_FullTime <= '0';
								En_St0 <= '0';
								En_St1 <= '0';
								En_St2 <= '0';
								En_St3 <= '0';
								FTMS<='1';
						
				when G0_St1 =>FTMS<='1';En_FullTime<='1';DoorLed<='1';	En_St1<='1';
				
				 if ModAuto = "00000001" then
							    Sel_Mod <= "01000";
							    Sel75 <= '1';
							    
							    
							    elsif ModAuto = "00000010" then
							    Sel_Mod <="00100";
							    Sel_PW <='1';
							    Sel60 <='1';
							   

							    elsif ModAuto = "00000100" then
							    Sel_Mod <= "00010";
							    Sel_PW <= '1';
							    Sel_XR <= '1';
							    Sel75 <= '1';
							  

							    elsif ModAuto = "00011000" then
							    Sel_Mod <="00001";
							    Sel_XR <= '1';
							    Sel50 <='1';
							    
							    elsif ModAuto = "00101000" then
							    Sel_Mod <= "00001";
							    Sel_XR <= '1';
							    Sel60 <= '1';
							   
							    elsif ModAuto = "01001000" then
							    Sel_Mod <= "00001";
							    Sel_XR <= '1';
							    Sel75 <= '1';
							  
						 else
							   Sel_PW <= PreWash;
							    Sel_XR <= ExtraRinse;
							   
							 
							    Sel_Mod <= "10000";
							    if Temp = "0110010" then 
							    Sel50 <= '1'; Sel60 <= '0' ; Sel75 <= '0';
							    elsif Temp = "0111100" then
							    Sel50 <= '0'; Sel60 <= '1' ; Sel75 <= '0';	
							    elsif Temp = "1001011" then
							    Sel50 <= '0'; Sel60 <= '0' ; Sel75 <= '1';
							    end if;
							   
							    end if;
							    
		
								 
					when G1_St1 =>	
					
					 if ModAuto = "00000001" then
							    Sel_Mod <= "01000";
							    Sel75 <= '1';
							    
							    
							    elsif ModAuto = "00000010" then
							    Sel_Mod <="00100";
							    Sel_PW <='1';
							    Sel60 <='1';
							   

							    elsif ModAuto = "00000100" then
							    Sel_Mod <= "00010";
							    Sel_PW <= '1';
							    Sel_XR <= '1';
							    Sel75 <= '1';
							  

							    elsif ModAuto = "00011000" then
							    Sel_Mod <="00001";
							    Sel_XR <= '1';
							    Sel50 <='1';
							    
							    elsif ModAuto = "00101000" then
							    Sel_Mod <= "00001";
							    Sel_XR <= '1';
							    Sel60 <= '1';
							   
							    elsif ModAuto = "01001000" then
							    Sel_Mod <= "00001";
							    Sel_XR <= '1';
							    Sel75 <= '1';
							  
							 else
							   Sel_PW <= PreWash;
							    Sel_XR <= ExtraRinse;
							   
							 
							    Sel_Mod <= "10000";
							    if Temp = "0110010" then 
							    Sel50 <= '1'; Sel60 <= '0' ; Sel75 <= '0';
							    elsif Temp = "0111100" then
							    Sel50 <= '0'; Sel60 <= '1' ; Sel75 <= '0';	
							    elsif Temp = "1001011" then
							    Sel50 <= '0'; Sel60 <= '0' ; Sel75 <= '1';
							    end if;
							   
							    end if;
							    En_FullTime <= '0';
								En_St0 <= '0';
								En_St1 <= '0';
								En_St2 <= '0';
								En_St3 <= '0';
								FTMS<='1';
						
				when H0_St2 =>  FTMS<='1';En_FullTime<='1';DoorLed<='1';En_St2<='1';
				
					if ModAuto = "00000001" then
							    Sel_Mod <= "01000";
							    Sel75 <= '1';
							    
							    
							    elsif ModAuto = "00000010" then
							    Sel_Mod <="00100";
							    Sel_PW <='1';
							    Sel60 <='1';
							   

							    elsif ModAuto = "00000100" then
							    Sel_Mod <= "00010";
							    Sel_PW <= '1';
							    Sel_XR <= '1';
							    Sel75 <= '1';
							  

							    elsif ModAuto = "00011000" then
							    Sel_Mod <="00001";
							    Sel_XR <= '1';
							    Sel50 <='1';
							    
							    elsif ModAuto = "00101000" then
							    Sel_Mod <= "00001";
							    Sel_XR <= '1';
							    Sel60 <= '1';
							   
							    elsif ModAuto = "01001000" then
							    Sel_Mod <= "00001";
							    Sel_XR <= '1';
							    Sel75 <= '1';
							  
						 else
							   Sel_PW <= PreWash;
							    Sel_XR <= ExtraRinse;
							   
							 
							    Sel_Mod <= "10000";
							    if Temp = "0110010" then 
							    Sel50 <= '1'; Sel60 <= '0' ; Sel75 <= '0';
							    elsif Temp = "0111100" then
							    Sel50 <= '0'; Sel60 <= '1' ; Sel75 <= '0';	
							    elsif Temp = "1001011" then
							    Sel50 <= '0'; Sel60 <= '0' ; Sel75 <= '1';
							    end if;
							   
							    end if;
				
			
								 
					when H1_St2 => 
					
					if ModAuto = "00000001" then
							    Sel_Mod <= "01000";
							    Sel75 <= '1';
							    
							    
							    elsif ModAuto = "00000010" then
							    Sel_Mod <="00100";
							    Sel_PW <='1';
							    Sel60 <='1';
							   

							    elsif ModAuto = "00000100" then
							    Sel_Mod <= "00010";
							    Sel_PW <= '1';
							    Sel_XR <= '1';
							    Sel75 <= '1';
							  

							    elsif ModAuto = "00011000" then
							    Sel_Mod <="00001";
							    Sel_XR <= '1';
							    Sel50 <='1';
							    
							    elsif ModAuto = "00101000" then
							    Sel_Mod <= "00001";
							    Sel_XR <= '1';
							    Sel60 <= '1';
							   
							    elsif ModAuto = "01001000" then
							    Sel_Mod <= "00001";
							    Sel_XR <= '1';
							    Sel75 <= '1';
							  
						 else
							   Sel_PW <= PreWash;
							    Sel_XR <= ExtraRinse;
							   
							 
							    Sel_Mod <= "10000";
							    if Temp = "0110010" then 
							    Sel50 <= '1'; Sel60 <= '0' ; Sel75 <= '0';
							    elsif Temp = "0111100" then
							    Sel50 <= '0'; Sel60 <= '1' ; Sel75 <= '0';	
							    elsif Temp = "1001011" then
							    Sel50 <= '0'; Sel60 <= '0' ; Sel75 <= '1';
							    end if;
							   
							    end if;
					En_FullTime <= '0';
								En_St0 <= '0';
								En_St1 <= '0';
								En_St2 <= '0';
								En_St3 <= '0';
								FTMS<='1';

					when I0_St3 =>FTMS<='1';En_FullTime<='1';DoorLed<='1';
						En_St3<='1';
					
					if ModAuto = "00000001" then
							    Sel_Mod <= "01000";
							    Sel75 <= '1';
							    
							    
							    elsif ModAuto = "00000010" then
							    Sel_Mod <="00100";
							    Sel_PW <='1';
							    Sel60 <='1';
							   

							    elsif ModAuto = "00000100" then
							    Sel_Mod <= "00010";
							    Sel_PW <= '1';
							    Sel_XR <= '1';
							    Sel75 <= '1';
							  

							    elsif ModAuto = "00011000" then
							    Sel_Mod <="00001";
							    Sel_XR <= '1';
							    Sel50 <='1';
							    
							    elsif ModAuto = "00101000" then
							    Sel_Mod <= "00001";
							    Sel_XR <= '1';
							    Sel60 <= '1';
							   
							    elsif ModAuto = "01001000" then
							    Sel_Mod <= "00001";
							    Sel_XR <= '1';
							    Sel75 <= '1';
							 else
							   Sel_PW <= PreWash;
							    Sel_XR <= ExtraRinse;
							   
							 
							    Sel_Mod <= "10000";
							    if Temp = "0110010" then 
							    Sel50 <= '1'; Sel60 <= '0' ; Sel75 <= '0';
							    elsif Temp = "0111100" then
							    Sel50 <= '0'; Sel60 <= '1' ; Sel75 <= '0';	
							    elsif Temp = "1001011" then
							    Sel50 <= '0'; Sel60 <= '0' ; Sel75 <= '1';
							    end if;
							   
							    end if;
					
								 
					when I1_St3 =>	
				
					if ModAuto = "00000001" then
							    Sel_Mod <= "01000";
							    Sel75 <= '1';
							    
							    
							    elsif ModAuto = "00000010" then
							    Sel_Mod <="00100";
							    Sel_PW <='1';
							    Sel60 <='1';
							   

							    elsif ModAuto = "00000100" then
							    Sel_Mod <= "00010";
							    Sel_PW <= '1';
							    Sel_XR <= '1';
							    Sel75 <= '1';
							  

							    elsif ModAuto = "00011000" then
							    Sel_Mod <="00001";
							    Sel_XR <= '1';
							    Sel50 <='1';
							    
							    elsif ModAuto = "00101000" then
							    Sel_Mod <= "00001";
							    Sel_XR <= '1';
							    Sel60 <= '1';
							   
							    elsif ModAuto = "01001000" then
							    Sel_Mod <= "00001";
							    Sel_XR <= '1';
							    Sel75 <= '1';
							  
						 else
							   Sel_PW <= PreWash;
							    Sel_XR <= ExtraRinse;
							   
							 
							    Sel_Mod <= "10000";
							    if Temp = "0110010" then 
							    Sel50 <= '1'; Sel60 <= '0' ; Sel75 <= '0';
							    elsif Temp = "0111100" then
							    Sel50 <= '0'; Sel60 <= '1' ; Sel75 <= '0';	
							    elsif Temp = "1001011" then
							    Sel50 <= '0'; Sel60 <= '0' ; Sel75 <= '1';
							    end if;
							   
							    end if;
					En_FullTime <= '0';
								En_St0 <= '0';
								En_St1 <= '0';
								En_St2 <= '0';
								En_St3 <= '0';
								FTMS<='1';
					when J_Done =>
					Finish<='1';
					FTMS<='1';
					En_FullTime<='0';
					if ModAuto = "00000001" then
							    Sel_Mod <= "01000";
							    Sel75 <= '1';
							    
							    
							    elsif ModAuto = "00000010" then
							    Sel_Mod <="00100";
							    Sel_PW <='1';
							    Sel60 <='1';
							   

							    elsif ModAuto = "00000100" then
							    Sel_Mod <= "00010";
							    Sel_PW <= '1';
							    Sel_XR <= '1';
							    Sel75 <= '1';
							  

							    elsif ModAuto = "00011000" then
							    Sel_Mod <="00001";
							    Sel_XR <= '1';
							    Sel50 <='1';
							    
							    elsif ModAuto = "00101000" then
							    Sel_Mod <= "00001";
							    Sel_XR <= '1';
							    Sel60 <= '1';
							   
							    elsif ModAuto = "01001000" then
							    Sel_Mod <= "00001";
							    Sel_XR <= '1';
							    Sel75 <= '1';
							  
						 else
							   Sel_PW <= PreWash;
							    Sel_XR <= ExtraRinse;
							   
							 
							    Sel_Mod <= "10000";
							    if Temp = "0110010" then 
							    Sel50 <= '1'; Sel60 <= '0' ; Sel75 <= '0';
							    elsif Temp = "0111100" then
							    Sel50 <= '0'; Sel60 <= '1' ; Sel75 <= '0';	
							    elsif Temp = "1001011" then
							    Sel50 <= '0'; Sel60 <= '0' ; Sel75 <= '1';
							    end if;
							   
							    end if;
				end case;

			end process Iesire;

END TypeArchitecture;

// VHDL entity mux_final_time, as the project stores it:
--------------------------------------------------------------------------------
-- Project :
-- File    :
-- Autor   : Ricu Razvan
-- Date    :
--
--------------------------------------------------------------------------------
-- Description :
--
--------------------------------------------------------------------------------

LIBRARY ieee;
USE ieee.std_logic_1164.all;

ENTITY mux_final_time IS
  PORT (
  FullTime:in std_logic_vector(7 downto 0);
  TimpNumarator:in std_logic_vector(7 downto 0);
  Ok_Button: in std_logic;
  TimpAfisor:out std_logic_vector(7 downto 0)
    );
END mux_final_time;


ARCHITECTURE TypeArchitecture OF mux_final_time IS
signal  t1 : std_logic_vector (7 downto 0) := "00000000";


BEGIN
	with Ok_Button select TimpAfisor <=
	FullTime when '0',
	TimpNumarator when '1',
	"00000000" when others; 
END TypeArchitecture;

// VHDL entity MUX_STAGE0_TIME, as the project stores it:
--------------------------------------------------------------------------------
-- Project :
-- File    :
-- Autor   : Ricu Razvan
-- Date    :
--
--------------------------------------------------------------------------------
-- Description :
--
--------------------------------------------------------------------------------

LIBRARY ieee;
USE ieee.std_logic_1164.all;

ENTITY MUX_STAGE0_TIME IS
  PORT (
  Stage0Time_Auto:in std_logic_vector(7 downto 0);
    Stage0Time_Manual:in std_logic_vector(7 downto 0);
    Enable_Manual: in std_logic;
    Stage0time: out std_logic_vector(7 downto 0)
    );
END MUX_STAGE0_TIME;

--------------------------------------------------------------------------------
--Complete your VHDL description below
--------------------------------------------------------------------------------

ARCHITECTURE TypeArchitecture OF MUX_STAGE0_TIME IS

signal  t1 : std_logic_vector (7 downto 0) := "00000000";

BEGIN
	with Enable_Manual select Stage0time <=
	Stage0Time_Manual when '1',
	Stage0Time_Auto when '0',
	"00000000" when others; 
END TypeArchitecture;

// VHDL entity Mux_Temperature, as the project stores it:
--------------------------------------------------------------------------------
-- Project :
-- File    :
-- Autor   : Ricu Razvan
-- Date    :
--
--------------------------------------------------------------------------------
-- Description :
--
--------------------------------------------------------------------------------

LIBRARY ieee;
USE ieee.std_logic_1164.all;

ENTITY Mux_Temperature IS
  PORT (
   TempAuto: in std_logic_vector(6 downto 0);
   TempManual: in std_logic_vector(6 downto 0);
   Enable_Manual: in std_logic;
Temp:out std_logic_vector(6 downto 0)
   
    );
END Mux_Temperature;

--------------------------------------------------------------------------------
--Complete your VHDL description below
--------------------------------------------------------------------------------

ARCHITECTURE TypeArchitecture OF Mux_Temperature IS

signal  t1 : std_logic_vector (6 downto 0) := "0000000";




BEGIN

	with Enable_Manual select Temp <=
	TempManual when '1',
	TempAuto when '0',
	"0000000" when others; 
END TypeArchitecture;

// VHDL entity CodificatorAuto, as the project stores it:
--------------------------------------------------------------------------------
-- Project :
-- File    :
-- Autor   : Moga Eduard
-- Date    :
--
--------------------------------------------------------------------------------
-- Description :
--
--------------------------------------------------------------------------------

LIBRARY ieee;
USE ieee.std_logic_1164.all;
USE ieee.std_logic_unsigned.all;

ENTITY CodificatorAuto IS
  PORT (
  		En : in std_logic;
  		Mods :  in std_logic_vector (3 downto 0);
 		Temp : in std_logic_vector ( 2 downto 0);
 		

		InformatieTM : out std_logic_vector (7 downto 0)
    );
END CodificatorAuto;



ARCHITECTURE TypeArchitecture OF CodificatorAuto IS

signal semnal : std_logic_vector (7 downto 0):= (others => '0');
signal semnal2 : std_logic_vector (7 downto 0) := (others => '0');
signal semnal3 : std_logic_vector (7 downto 0) := (others => '0');
signal ok : std_logic := '0';
BEGIN

	process(En, Mods)
	variable info : std_logic_vector(7 downto 0) := (others => '0');
		begin 
				if En = '0' then info := (others => '1');
				ok <= '0';
				else

					case Mods is 

					when "0001" => info := "00000001"; ok <= '0';
					when "0010" => info := "00000010"; ok <= '0';
					when "0100" => info := "00000100"; ok <= '0';
					when "1000" => info := "00001000"; ok <= '1';
					when others => info:= "11111111"; ok <= '0';
					end case;
					
				end if;
				semnal <= info;
				
		end process;

	process(En,Temp)
	variable info : std_logic_vector(7 downto 0) := (others => '1');
	
		begin

		if En = '0' then info := "00000000";
		else
			if ok = '1' then 
				case Temp is
				when "001" => info := "00010000";
				when "010" => info := "00100000";
				when "100" => info := "01000000";
				when others => info := "00000000";
				end case;
			else
				info := "00000000";
			end if;
	 	end if;

		
			semnal2 <= info;

		end process;

semnal3 <= semnal + semnal2;

InformatieTM <= semnal3;
END TypeArchitecture;

// VHDL entity DecoderAuto, as the project stores it:
--------------------------------------------------------------------------------
-- Project :
-- File    :
-- Autor   : Moga Eduard
-- Date    :
--
--------------------------------------------------------------------------------
-- Description :
--
--------------------------------------------------------------------------------

LIBRARY ieee;
USE ieee.std_logic_1164.all;

ENTITY DecoderAuto IS
  PORT (
	
	StringCod : in std_logic_vector (7 downto 0);
	TimeStage0 : out std_logic_vector (7 downto 0);
	TimeStage1 : out std_logic_vector (7 downto 0);	
     TimeStage2 : out std_logic_vector (7 downto 0);
    	TimeStage3 : out std_logic_vector (7 downto 0);
    	FullTime 	 : out std_logic_vector (7 downto 0);
    	Temp		 : out std_logic_vector (6 downto 0)	
	    );
END DecoderAuto;



ARCHITECTURE TypeArchitecture OF DecoderAuto IS

signal t0 : std_logic_vector (7 downto 0);
signal t1 : std_logic_vector (7 downto 0);
signal t2 : std_logic_vector (7 downto 0);
signal t3 : std_logic_vector (7 downto 0);
signal tful : std_logic_vector (7 downto 0);
signal tmp : std_logic_vector (6 downto 0);
BEGIN

	process(StringCod)
	variable aux : std_logic_vector (7 downto 0) := (others => '0');
	variable aux2 : std_logic_vector (7 downto 0) := (others => '0');
	variable aux3 : std_logic_vector (7 downto 0) := (others => '0');
	variable aux4 : std_logic_vector (7 downto 0) := (others => '0');
	variable aux5 : std_logic_vector (7 downto 0) := (others => '0');
	variable aux6 : std_logic_vector (6 downto 0) := (others => '0');
		begin

			case StringCod is 
				when "11111111" => aux := (others => '0');
							    aux2 := (others => '0');
							    aux3 := (others => '0');
							    aux4 := (others => '0');
							    aux5 := (others => '0');
							    aux6 := (others => '0');
							    
				when "00000001" => aux :=  "00000100";			-- stage0
							    aux2 := "00110001";			-- stage1
							    aux3 := "00000101";			-- stage2
							    aux4 := "00000000";			-- stage3
							    aux5 := "00111010";			-- FULLTIME
							    aux6 := "1001011";			-- temp
							    
				when "00000010" => aux :=  "00001110";
							    aux2 := "00100010";
							    aux3 := "10000101";
							    aux4 := "00011100";
							    aux5 := "11010010";
							    aux6 := "0111100";
							    
				when "00000100" => aux :=  "00001110";
							    aux2 := "00110001";
							    aux3 := "01010011";
							    aux4 := "00011100";
							    aux5 := "10101111";
							    aux6 := "1001011";
							    
				when "00011000" => aux :=  "00000100";
							    aux2 := "00011000";
							    aux3 := "01011101";
							    aux4 := "00011100";
							    aux5 := "10010110";
							    aux6 := "0110010";
							    
				when "00101000" => aux :=  "00000100";
							    aux2 := "00100010";
							    aux3 := "01010011";
							    aux4 := "00011100";
							    aux5 := "10010110";						
							    aux6 := "0111100";
							    
				when "01001000" => aux :=  "00000100";
							    aux2 := "00110001";
							    aux3 := "01000100";
							    aux4 := "00011100";
							    aux5 := "10010110";
							    aux6 := "1001011";
							    
				when others 	=>   aux := (others => '0');
							    aux2 := (others => '0');
							    aux3 := (others => '0');
							    aux4 := (others => '0');
							    aux5 := (others => '0');
							    aux6 := (others => '0');
							    			    			    
							    			 
			end case;

				t0 <= aux;
				t1 <= aux2;
				t2 <= aux3;
				t3 <= aux4;
				tful <= aux5;
				tmp <= aux6;
		end process;

		TimeStage0 <= t0;
		TimeStage1 <= t1;
		TimeStage2 <= t2;
		TimeStage3 <= t3;
		FullTime <= tful;
		Temp <= tmp;

END TypeArchitecture;

// VHDL entity converter, as the project stores it:
--------------------------------------------------------------------------------
-- Project :
-- File    :
-- Autor   : Moga Eduard
-- Date    :
--
--------------------------------------------------------------------------------
-- Description :
--
--------------------------------------------------------------------------------

LIBRARY ieee;
USE ieee.std_logic_1164.all;
USE ieee.numeric_std.all;

USE ieee.std_logic_unsigned.all;
ENTITY converter IS
  PORT (
 		A : in std_logic_vector (7 downto 0);

 		n1 : out std_logic_vector (3 downto 0);
 		n2 : out std_logic_vector (3 downto 0);
 		n3 : out std_logic_vector (3 downto 0)
    );
END converter;





ARCHITECTURE TypeArchitecture OF converter IS
signal cif1 : std_logic_vector(3 downto 0) := "0000";
signal cif2 : std_logic_vector(3 downto 0) := "0000";
signal cif3 : std_logic_vector(3 downto 0) := "0000";


signal int : integer := 0;
signal aux : integer :=0;
signal o1  : integer := 0;
signal o2  : integer := 0;
signal o3  : integer := 0;


BEGIN

	--o1 <= to_integer(unsigned(A));
	--o2 <= o1 mod 10;
	--o3 <= o1 / 10;
	--cif1 <= std_logic_vector(to_unsigned(o2,cif1'length));
	--cif2 <= std_logic_vector(to_unsigned(o3,cif2'length));
	--n1 <= cif1;
	--n2 <= cif2;

	int <= to_integer(unsigned(A));

	o1 <= int mod 10;
	aux <= int / 10;
	o2 <= aux mod 10;
	o3 <= aux /10;

	cif1 <= std_logic_vector(to_unsigned(o1,cif1'length));
	cif2 <= std_logic_vector(to_unsigned(o2,cif2'length));
	cif3 <= std_logic_vector(to_unsigned(o3,cif3'length));

	n1 <= cif1;
	n2 <= cif2;
	n3 <= cif3;
	



END TypeArchitecture;

// VHDL entity muxfinaltime2, as the project stores it:
--------------------------------------------------------------------------------
-- Project :
-- File    :
-- Autor   : Moga Eduard
-- Date    :
--
--------------------------------------------------------------------------------
-- Description :
--
--------------------------------------------------------------------------------

LIBRARY ieee;
USE ieee.std_logic_1164.all;

ENTITY muxfinaltime2 IS
  PORT (
  FullTimeAuto:in std_logic_vector(7 downto 0);
  FullTimeManual:in std_logic_vector(7 downto 0);
  Enable_Manual: in std_logic;
  FullTime:out std_logic_vector(7 downto 0)
    );
END muxfinaltime2;


ARCHITECTURE TypeArchitecture OF muxfinaltime2 IS
signal  t1 : std_logic_vector (7 downto 0) := "00000000";


BEGIN
	with Enable_Manual select FullTime <=
	FullTimeAuto when '0',
	FullTimeManual when '1',
	"00000000" when others; 
END TypeArchitecture;

// VHDL entity ssd_lit, as the project stores it:
--------------------------------------------------------------------------------
-- Project :
-- File    :
-- Autor   :
 --Moga Eduard
-- Date    :
--
--------------------------------------------------------------------------------
-- Description :
--
 --Un SSD care afiseaza Error(ERR) in caz de selectare gresita a modurilor(Pentru Optimizari si Update-uri viitoare) 
-- Acesta trebuie conectat la un mux cu afisorul de timp pentru a selecta in functie de stagiul in care ne aflam care dintre valori vrem sa le afisam
--------------------------------------------------------------------------------

LIBRARY ieee;
USE ieee.std_logic_1164.all;

USE ieee.std_logic_unsigned.all;
ENTITY ssd_lit IS
  PORT (
  	input : in std_logic;
  	CLK   : in std_logic;
  	anod	 : out std_logic_vector (2 downto 0);
  	catod : out std_logic_vector (6 downto 0)
    );
END ssd_lit;


ARCHITECTURE TypeArchitecture OF ssd_lit IS

signal poz : std_logic_vector (2 downto 0) :="000";
signal l1 : std_logic_vector (3 downto 0) := "0001";
signal l2 : std_logic_vector (3 downto 0) := "0010";
signal litera : std_logic_vector (3 downto 0) := "0000";
BEGIN

	process(CLK)
		begin
			if rising_edge(CLK) then
				poz <= poz +1;
			end if;
			
		end process;

	process(poz)
		begin

			case poz is 
				when "001" =>
					anod <= "100";
					litera <= l1;
				when "010" =>
					anod <= "010";
					litera <= l2;
				when "011" =>
					anod <= "001";
					litera <= l2;
		
				when others =>
					anod <="000";
			end case;

		end process;


	process(litera)
		begin
			if input = '0' then
				case litera is 
					when "0001" =>
						catod <= "1111001";
					when "0010" =>
						catod <= "1010000";
					when others =>
						catod <="0000000";
				end case;
			else
				catod <="0000000";
			 end if;
				


		end process;
	
	

END TypeArchitecture;
